# Fritzing sketch RTC TIMER (saved by Fritzing 0.9.3b)

parts:
  Part1 = Arduino Mega ADK (Rev3)
  Part2 = Real Time Clock Module - DS1307 RTC Breakout Board

nets:
  N1: Part1.A4, Part2.SDA
  N2: Part1.A5, Part2.SCL
  5V: Part1.5V, Part2.5V
  GND: Part1.GND, Part2.GND
